# Fritzing sketch circuit (saved by Fritzing 0.9.3b)
breadboards: 1
stripboards: 1

parts:
  Εξάρτημα1 = Arduino Mega 2560 (Rev3)
  LCD2004-I2C1 = LCD2004-I2C
  DHT-11 = KY-015 Temperature & Humidity Sensor Module [package="Breakout board"]
  Reed_Switch = Magnetic Door Switch [part_number="Διακόπτης παραθύρου" package=reed_switch_plastic]
  CCS_811 = Adafruit CCS811 [part_number="Adafruit #3566"]
  HC-05 = Bluetooth HC-05 Macho
  R1 = Resistor [tolerance=±5% resistance=2.2k package=THT]
  R2 = Resistor [tolerance=±5% resistance=4.7k package=THT]
  LM1117_Regulator = V_REG_LD1117VXX [package=78xxl]
  PM_Breakout = mystery part, 6 pins [chip_label="PM BREAKOUT"]
  Καλωδιοταινία = KENT_LCD_CONN [package=ffc_16]
  U3 = KENT_LCD_CONN [package=ffc_16]
  R3 = Resistor [tolerance=±5% resistance=220 package=THT]
  R4 = Resistor [tolerance=±5% resistance=220 package=THT]
  R5 = Resistor [tolerance=±5% resistance=220 package=THT]
  R6 = Resistor [tolerance=±5% resistance=220 package=THT]
  R7 = Resistor [tolerance=±5% resistance=220 package=THT]
  R8 = Resistor [tolerance=±5% resistance=220 package=THT]
  Κλιματισμός = LED - 5mm [color="Red (633nm)" package="5 mm [THT]"]
  LED2 = LED - 5mm [color="Green (555nm)" package="5 mm [THT]"]
  Καθαριστής_Αέρα = LED - 5mm [color="Red (633nm)" package="5 mm [THT]"]
  LED3 = LED - 5mm [color="Blue (430nm)" package="5 mm [THT]"]
  Καλοριφέρ = LED - 5mm [color="Red (633nm)" package="5 mm [THT]"]
  LED4 = LED - 5mm [color="Blue (430nm)" package="5 mm [THT]"]
  Φωτοκύτταρο = Photocell (LDR) [package=THT]
  R9 = Resistor [tolerance=±5% resistance=10k package=THT]
  Φωτισμός = LED - 5mm [color="White (4500K)" package="5 mm [THT]"]
  R10 = Resistor [tolerance=±5% resistance=100 package=THT]

nets:
  N1: Εξάρτημα1.A8, Φωτοκύτταρο.pin_1, R9.Pin_1
  N2: Εξάρτημα1.D21/SCL, LCD2004-I2C1.SCL, CCS_811.SCL
  N3: Εξάρτημα1.D20/SDA, LCD2004-I2C1.SDA, CCS_811.SDA
  N4: Εξάρτημα1.D19/RX1, PM_Breakout.pin4
  N5: Εξάρτημα1.D18/TX1, PM_Breakout.pin3
  N6: Εξάρτημα1.D10_PWM, Reed_Switch.2
  VCC: Εξάρτημα1.5V, LCD2004-I2C1.VCC, DHT-11.Vin, HC-05.VCC, LM1117_Regulator.IN, PM_Breakout.pin1, Φωτοκύτταρο.pin_0
  GND: Εξάρτημα1.GND, LCD2004-I2C1.GND, DHT-11.-, Reed_Switch.1, CCS_811.GND, HC-05.GND, R2.Pin_1, LM1117_Regulator.GND, PM_Breakout.pin2, R3.Pin_0, R4.Pin_0, R5.Pin_0, R6.Pin_0, R7.Pin_0, R8.Pin_0, R9.Pin_0, R10.Pin_0
  N7: Εξάρτημα1.D0_RX0, HC-05.TXD
  N8: Εξάρτημα1.D1_TX0, R1.Pin_1
  N9: Εξάρτημα1.D2_PWM, DHT-11.S
  N10: Εξάρτημα1.D31, Καθαριστής_Αέρα.anode
  N11: Εξάρτημα1.D33, LED3.anode
  N12: Εξάρτημα1.D35, LED2.anode
  N13: Εξάρτημα1.D37, Κλιματισμός.anode
  N14: Εξάρτημα1.D39, Καλοριφέρ.anode
  N15: Εξάρτημα1.D41, LED4.anode
  N16: Εξάρτημα1.D50, Φωτισμός.anode
  N17: CCS_811.3.3V, LM1117_Regulator.OUT
  N18: HC-05.RXD, R1.Pin_0, R2.Pin_0
  N19: Καλωδιοταινία._RESET, U3.VSS2, U3.VCC
  N20: Καλωδιοταινία.BUSY, U3.CS, U3.VPWR1
  N21: Καλωδιοταινία.VSS1, U3.SI, U3.VPWR2
  N22: Καλωδιοταινία.SCK, U3.SO, U3.VSS3
  N23: Καλωδιοταινία.SO, U3.SCK, U3.VPWR3
  N24: Καλωδιοταινία.SI, U3.VSS1, U3.VSS4
  N25: Καλωδιοταινία.CS, U3.BUSY, U3.NC1
  N26: Καλωδιοταινία.VSS2, U3._RESET, U3.NC2
  N27: R3.Pin_1, LED2.cathode
  N28: R4.Pin_1, LED4.cathode
  N29: R5.Pin_1, Καλοριφέρ.cathode
  N30: R6.Pin_1, Καθαριστής_Αέρα.cathode
  N31: R7.Pin_1, LED3.cathode
  N32: R8.Pin_1, Κλιματισμός.cathode
  N33: Φωτισμός.cathode, R10.Pin_1

notes:
  PM Breakout Pins:
  1-> 5V
  2-> GND
  3-> TX
  4-> RX
  5-> RESET
  6-> EN

custom parts:
  LCD2004-I2C: A standard character display with 4x20 characters. Comes in many colors with LCM2004 IIC attached.
  KY-015 Temperature & Humidity Sensor Module: KY-015 temperature and humidity sensor module, provides a low-latency serial interface to measure humidity and temperature.
  Adafruit CCS811: Breathe easy - we finally have an I2C VOC/eCO2 sensor in the Adafruit shop! Add air quality monitoring to your project and with an Adafruit CCS811 Air Quality Sensor Breakout. This sensor from AMS is a gas sensor that can detect a wide range of Volatile Organic Compounds (VOCs) and is intended for indoor air quality monitoring. When connected to your microcontroller (running our library code)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
